// Logisim project C-ControlUnit.circ as structural Verilog
module ControlUnit (
  input  RST,
  input  CLK,
  input  [5:0] CODE,
  input  End_Fectch_Instruction,
  input  Instruction_Avaiable,
  output Start_Fectch_Instruction,
  output STOP,
  output LoadInstructionRegister,
  output Load_PC,
  output TTY_ENABLE,
  output [3:0] ALU_OP_SELECTOR,
  output WRITE_RF,
  output [1:0] ALU_SELECTOR_A,
  output [1:0] ADDRESS_SELECTOR,
  output [1:0] ALU_SELECTOR_B,
  output [1:0] DATA_SELECTOR,
  output LOAD_HI,
  output LOAD_LO
);

  wire ADD, ADDI, AND, ANDI, BEQ, BGTZ, BLEZ, BLTZ, BNE, d_ff_1_q, demultiplexer_1_out0,
       demultiplexer_1_out1, demultiplexer_2_out0, demultiplexer_2_out1, DIV, DIVU, END_ADD, END_HALT,
       END_NOP, END_TTY, Forward_PC, HALT, INVALID, J, JR, KBD, LW, MFHI, MFLO, MULT, MULTU, NOP, NOR, OR,
       or_1_out, or_3_out, or_5_out, ORI, POP, PUSH, RND, Single_Cycle, SLT, SLTU, STLI, STLIU, SUB, SW, TTY,
       Wait_for_instruction_fetch_q, XOR, XORI;

  or or_1 (or_1_out, 1'b0, demultiplexer_1_out1);
  D_Flip_Flop d_ff_1 (.clk(CLK), .D(or_1_out), .Q(d_ff_1_q), .preset(RST));  // open: Qn, en, reset
  Demultiplexer #(.enable("false")) demultiplexer_1 (
    .out0(demultiplexer_1_out0), .out1(demultiplexer_1_out1), .in(d_ff_1_q), .sel(RST));
  or or_2 (Start_Fectch_Instruction, Single_Cycle, demultiplexer_1_out0);
  D_Flip_Flop Wait_for_instruction_fetch (
    .clk(CLK), .D(or_3_out), .Q(Wait_for_instruction_fetch_q), .reset(RST));  // open: Qn, preset, en
  or or_3 (or_3_out, demultiplexer_2_out0, Start_Fectch_Instruction);
  Demultiplexer #(.enable("false")) demultiplexer_2 (
    .out0(demultiplexer_2_out0), .out1(demultiplexer_2_out1), .in(Wait_for_instruction_fetch_q),
    .sel(End_Fectch_Instruction));
  _6bitDemultiplexer u_6bitdemultiplexer_1 (
    .Power(demultiplexer_2_out1), ._6bit_Selector(CODE), .Output_0(NOP), .Output_1(BLTZ), .Output_2(J),
    .Output_3(JR), .Output_4(BEQ), .Output_5(BNE), .Output_6(BLEZ), .Output_7(BGTZ), .Output_8(ADDI),
    .Output_10(STLI), .Output_11(STLIU), .Output_12(ANDI), .Output_13(ORI), .Output_14(XORI),
    .Output_16(MFHI), .Output_18(MFLO), .Output_24(MULT), .Output_25(MULTU), .Output_26(DIV),
    .Output_27(DIVU), .Output_31(INVALID), .Output_32(ADD), .Output_34(SUB), .Output_35(LW), .Output_36(AND),
    .Output_37(OR), .Output_39(NOR), .Output_40(XOR), .Output_41(SLTU), .Output_42(SLT), .Output_43(SW),
    .Output_48(POP), .Output_49(PUSH), .Output_57(TTY), .Output_58(RND), .Output_60(KBD), .Output_63(HALT));  // open: Output_9, Output_15, Output_17, Output_19, Output_20, Output_21, Output_22, Output_23, Output_28, Output_29, Output_30, Output_33, Output_38, Output_44, Output_45, Output_46, Output_47, Output_50, Output_51, Output_52, Output_53, Output_54, Output_55, Output_56, Output_59, Output_61, Output_62
  NOP nop_1 (.POWER_IN(NOP), .POWER_OUT(END_NOP));
  HALT halt_1 (.POWER_IN(HALT), .POWER_OUT(END_HALT));
  TTY tty_1 (.POWER_IN(TTY), .POWER_OUT(END_TTY), .TTY_ENABLE(TTY_ENABLE));
  or or_4 (Forward_PC, END_NOP, END_ADD, END_TTY);
  or or_5 (or_5_out, STOP, END_HALT);
  D_Flip_Flop Wait_a_cycle (.clk(CLK), .D(or_5_out), .Q(STOP), .reset(RST));  // open: Qn, preset, en
  FORWARD_PC forward_pc_1 (.POWER_IN(Forward_PC), .POWER_OUT(Single_Cycle), .Load_PC(Load_PC), .CLK(CLK), .RST(RST));
  ADD add_1 (
    .CLK(CLK), .RST(RST), .POWER_IN(ADD), .POWER_OUT(END_ADD), .ALU_SELECTOR_A0(ALU_SELECTOR_A[0]),
    .ALU_SELECTOR_B0(ALU_SELECTOR_B[0]), .WRITE_RF(WRITE_RF));

  assign ADDRESS_SELECTOR = 2'b00;
  assign ALU_OP_SELECTOR = 4'b0000;
  assign ALU_SELECTOR_A[1] = 1'b0;
  assign ALU_SELECTOR_B[1] = 1'b0;
  assign DATA_SELECTOR = 2'b00;
  assign LOAD_HI = 1'b0;
  assign LOAD_LO = 1'b0;
  assign LoadInstructionRegister = Instruction_Avaiable;

  // Other names for the same wires on the sheet: ALU_ADD_SELECTOR_A0 = ALU_SELECTOR_A[0];
  //   ALU_ADD_SELECTOR_B0 = ALU_SELECTOR_B[0]; End_fetch_instruction = End_Fectch_Instruction;
  //   Instruction_ready = Instruction_Avaiable; LOAD_PC_0 = Load_PC;
  //   Start_fetch_instruction = Start_Fectch_Instruction; TTY_ENBALE = TTY_ENABLE; WRITE_RF_ADD = WRITE_RF

  // Notes on the sheet:
  //   FetchInstruction
  //   TTY
  //   KBD
  //   ALU Operation
  //   Control Signals
  //   Fetch Instruction
  //   Decode Instruction
  //   Program Counter
  //   Execution
  //   Register File
  //   One Cycle Instructions
  //   HALT
  //   Algorithmic State Machines
endmodule

module ADD (
  input  CLK,
  input  RST,
  input  POWER_IN,
  output ALU_SELECTOR_A0,
  output ALU_SELECTOR_B0,
  output POWER_OUT,
  output WRITE_RF
);

  D_Flip_Flop d_ff_1 (.clk(CLK), .D(POWER_IN), .Q(POWER_OUT), .reset(RST));  // open: Qn, preset, en

  assign ALU_SELECTOR_A0 = POWER_IN;
  assign ALU_SELECTOR_B0 = POWER_IN;
  assign WRITE_RF = POWER_IN;
endmodule

module FORWARD_PC (
  input  CLK,
  input  RST,
  input  POWER_IN,
  output Load_PC,
  output POWER_OUT
);

  D_Flip_Flop d_ff_1 (.clk(CLK), .D(POWER_IN), .Q(POWER_OUT), .reset(RST));  // open: Qn, preset, en

  assign Load_PC = POWER_IN;
endmodule

module NOP (
  input  POWER_IN,
  output POWER_OUT
);


  assign POWER_OUT = POWER_IN;
endmodule

module TTY (
  input  POWER_IN,
  output TTY_ENABLE,
  output POWER_OUT
);


  assign POWER_OUT = POWER_IN;
  assign TTY_ENABLE = POWER_IN;
endmodule

module HALT (
  input  POWER_IN,
  output POWER_OUT
);


  assign POWER_OUT = POWER_IN;
endmodule
